// Logisim project Processor.circ as structural Verilog: 15 circuits, main circuit data_bus
module RegFile (
  input  write_enable,
  input  [31:0] rd_in,
  input  [4:0] rd_select,
  input  [4:0] rs_select,
  input  [4:0] rt_select,
  output [31:0] rs_out,
  output [31:0] rt_out
);

  wire clock_1_out, demultiplexer_1_out1, demultiplexer_1_out2, demultiplexer_1_out3, demultiplexer_1_out4,
       demultiplexer_1_out5, demultiplexer_1_out6, demultiplexer_1_out7, demultiplexer_1_out8,
       demultiplexer_1_out9, demultiplexer_1_out10, demultiplexer_1_out11, demultiplexer_1_out12,
       demultiplexer_1_out13, demultiplexer_1_out14, demultiplexer_1_out15, demultiplexer_1_out16,
       demultiplexer_1_out17, demultiplexer_1_out18, demultiplexer_1_out19, demultiplexer_1_out20,
       demultiplexer_1_out21, demultiplexer_1_out22, demultiplexer_1_out23, demultiplexer_1_out24,
       demultiplexer_1_out25, demultiplexer_1_out26, demultiplexer_1_out27, demultiplexer_1_out28,
       demultiplexer_1_out29, demultiplexer_1_out30, demultiplexer_1_out31;
  wire [31:0] at_q, demultiplexer_2_out1, demultiplexer_2_out2, demultiplexer_2_out3, demultiplexer_2_out4,
       demultiplexer_2_out5, demultiplexer_2_out6, demultiplexer_2_out7, demultiplexer_2_out8,
       demultiplexer_2_out9, demultiplexer_2_out10, demultiplexer_2_out11, demultiplexer_2_out12,
       demultiplexer_2_out13, demultiplexer_2_out14, demultiplexer_2_out15, demultiplexer_2_out16,
       demultiplexer_2_out17, demultiplexer_2_out18, demultiplexer_2_out19, demultiplexer_2_out20,
       demultiplexer_2_out21, demultiplexer_2_out22, demultiplexer_2_out23, demultiplexer_2_out24,
       demultiplexer_2_out25, demultiplexer_2_out26, demultiplexer_2_out27, demultiplexer_2_out28,
       demultiplexer_2_out29, demultiplexer_2_out30, demultiplexer_2_out31, fifteen_q, five_q, register_1_q,
       register_2_q, register_3_q, register_4_q, register_5_q, register_6_q, register_7_q, register_8_q,
       register_9_q, register_10_q, register_11_q, register_12_q, register_13_q, register_14_q,
       register_15_q, register_16_q, register_17_q, register_18_q, register_19_q, register_20_q,
       register_21_q, register_22_q, register_23_q, register_24_q, ten_q, thirty_q, twenty_q, twentyfive_q,
       v0_q;

  // Probe on rd_select
  Demultiplexer #(.select(5)) demultiplexer_1 (
    .out1(demultiplexer_1_out1), .out2(demultiplexer_1_out2), .out3(demultiplexer_1_out3),
    .out4(demultiplexer_1_out4), .out5(demultiplexer_1_out5), .out6(demultiplexer_1_out6),
    .out7(demultiplexer_1_out7), .out8(demultiplexer_1_out8), .out9(demultiplexer_1_out9),
    .out10(demultiplexer_1_out10), .out11(demultiplexer_1_out11), .out12(demultiplexer_1_out12),
    .out13(demultiplexer_1_out13), .out14(demultiplexer_1_out14), .out15(demultiplexer_1_out15),
    .out16(demultiplexer_1_out16), .out17(demultiplexer_1_out17), .out18(demultiplexer_1_out18),
    .out19(demultiplexer_1_out19), .out20(demultiplexer_1_out20), .out21(demultiplexer_1_out21),
    .out22(demultiplexer_1_out22), .out23(demultiplexer_1_out23), .out24(demultiplexer_1_out24),
    .out25(demultiplexer_1_out25), .out26(demultiplexer_1_out26), .out27(demultiplexer_1_out27),
    .out28(demultiplexer_1_out28), .out29(demultiplexer_1_out29), .out30(demultiplexer_1_out30),
    .out31(demultiplexer_1_out31), .in(write_enable), .sel(rd_select));  // open: out0
  Demultiplexer #(.select(5), .width(32)) demultiplexer_2 (
    .out1(demultiplexer_2_out1), .out2(demultiplexer_2_out2), .out3(demultiplexer_2_out3),
    .out4(demultiplexer_2_out4), .out5(demultiplexer_2_out5), .out6(demultiplexer_2_out6),
    .out7(demultiplexer_2_out7), .out8(demultiplexer_2_out8), .out9(demultiplexer_2_out9),
    .out10(demultiplexer_2_out10), .out11(demultiplexer_2_out11), .out12(demultiplexer_2_out12),
    .out13(demultiplexer_2_out13), .out14(demultiplexer_2_out14), .out15(demultiplexer_2_out15),
    .out16(demultiplexer_2_out16), .out17(demultiplexer_2_out17), .out18(demultiplexer_2_out18),
    .out19(demultiplexer_2_out19), .out20(demultiplexer_2_out20), .out21(demultiplexer_2_out21),
    .out22(demultiplexer_2_out22), .out23(demultiplexer_2_out23), .out24(demultiplexer_2_out24),
    .out25(demultiplexer_2_out25), .out26(demultiplexer_2_out26), .out27(demultiplexer_2_out27),
    .out28(demultiplexer_2_out28), .out29(demultiplexer_2_out29), .out30(demultiplexer_2_out30),
    .out31(demultiplexer_2_out31), .in(rd_in), .sel(rd_select));  // open: out0
  // Probe on rd_in
  Register #(.width(32)) v0 (
    .D(demultiplexer_2_out2), .en(demultiplexer_1_out2), .clk(clock_1_out), .Q(v0_q));  // open: clr
  Register #(.width(32)) register_1 (
    .D(demultiplexer_2_out4), .en(demultiplexer_1_out4), .clk(clock_1_out), .Q(register_1_q));  // open: clr
  Register #(.width(32)) register_2 (
    .D(demultiplexer_2_out6), .en(demultiplexer_1_out6), .clk(clock_1_out), .Q(register_2_q));  // open: clr
  Register #(.width(32)) register_3 (
    .D(demultiplexer_2_out8), .en(demultiplexer_1_out8), .clk(clock_1_out), .Q(register_3_q));  // open: clr
  Register #(.width(32)) at (
    .D(demultiplexer_2_out1), .en(demultiplexer_1_out1), .clk(clock_1_out), .Q(at_q));  // open: clr
  Register #(.width(32)) register_4 (
    .D(demultiplexer_2_out3), .en(demultiplexer_1_out3), .clk(clock_1_out), .Q(register_4_q));  // open: clr
  Register #(.width(32)) five (
    .D(demultiplexer_2_out5), .en(demultiplexer_1_out5), .clk(clock_1_out), .Q(five_q));  // open: clr
  Register #(.width(32)) register_5 (
    .D(demultiplexer_2_out7), .en(demultiplexer_1_out7), .clk(clock_1_out), .Q(register_5_q));  // open: clr
  Register #(.width(32)) ten (
    .D(demultiplexer_2_out10), .en(demultiplexer_1_out10), .clk(clock_1_out), .Q(ten_q));  // open: clr
  Register #(.width(32)) register_6 (
    .D(demultiplexer_2_out12), .en(demultiplexer_1_out12), .clk(clock_1_out), .Q(register_6_q));  // open: clr
  Register #(.width(32)) register_7 (
    .D(demultiplexer_2_out14), .en(demultiplexer_1_out14), .clk(clock_1_out), .Q(register_7_q));  // open: clr
  Register #(.width(32)) register_8 (
    .D(demultiplexer_2_out16), .en(demultiplexer_1_out16), .clk(clock_1_out), .Q(register_8_q));  // open: clr
  Register #(.width(32)) register_9 (
    .D(demultiplexer_2_out18), .en(demultiplexer_1_out18), .clk(clock_1_out), .Q(register_9_q));  // open: clr
  Register #(.width(32)) twenty (
    .D(demultiplexer_2_out20), .en(demultiplexer_1_out20), .clk(clock_1_out), .Q(twenty_q));  // open: clr
  Register #(.width(32)) register_10 (
    .D(demultiplexer_2_out22), .en(demultiplexer_1_out22), .clk(clock_1_out), .Q(register_10_q));  // open: clr
  Register #(.width(32)) register_11 (
    .D(demultiplexer_2_out24), .en(demultiplexer_1_out24), .clk(clock_1_out), .Q(register_11_q));  // open: clr
  Clock clock_1 (.out(clock_1_out));
  Register #(.width(32)) register_12 (
    .D(demultiplexer_2_out9), .en(demultiplexer_1_out9), .clk(clock_1_out), .Q(register_12_q));  // open: clr
  Register #(.width(32)) register_13 (
    .D(demultiplexer_2_out11), .en(demultiplexer_1_out11), .clk(clock_1_out), .Q(register_13_q));  // open: clr
  Register #(.width(32)) register_14 (
    .D(demultiplexer_2_out13), .en(demultiplexer_1_out13), .clk(clock_1_out), .Q(register_14_q));  // open: clr
  Register #(.width(32)) fifteen (
    .D(demultiplexer_2_out15), .en(demultiplexer_1_out15), .clk(clock_1_out), .Q(fifteen_q));  // open: clr
  Register #(.width(32)) register_15 (
    .D(demultiplexer_2_out17), .en(demultiplexer_1_out17), .clk(clock_1_out), .Q(register_15_q));  // open: clr
  Register #(.width(32)) register_16 (
    .D(demultiplexer_2_out19), .en(demultiplexer_1_out19), .clk(clock_1_out), .Q(register_16_q));  // open: clr
  Register #(.width(32)) register_17 (
    .D(demultiplexer_2_out21), .en(demultiplexer_1_out21), .clk(clock_1_out), .Q(register_17_q));  // open: clr
  Register #(.width(32)) register_18 (
    .D(demultiplexer_2_out23), .en(demultiplexer_1_out23), .clk(clock_1_out), .Q(register_18_q));  // open: clr
  Register #(.width(32)) register_19 (
    .D(demultiplexer_2_out26), .en(demultiplexer_1_out26), .clk(clock_1_out), .Q(register_19_q));  // open: clr
  Register #(.width(32)) register_20 (
    .D(demultiplexer_2_out28), .en(demultiplexer_1_out28), .clk(clock_1_out), .Q(register_20_q));  // open: clr
  Register #(.width(32)) thirty (
    .D(demultiplexer_2_out30), .en(demultiplexer_1_out30), .clk(clock_1_out), .Q(thirty_q));  // open: clr
  Register #(.width(32)) twentyfive (
    .D(demultiplexer_2_out25), .en(demultiplexer_1_out25), .clk(clock_1_out), .Q(twentyfive_q));  // open: clr
  Register #(.width(32)) register_21 (
    .D(demultiplexer_2_out27), .en(demultiplexer_1_out27), .clk(clock_1_out), .Q(register_21_q));  // open: clr
  Register #(.width(32)) register_22 (
    .D(demultiplexer_2_out29), .en(demultiplexer_1_out29), .clk(clock_1_out), .Q(register_22_q));  // open: clr
  Register #(.width(32)) register_23 (
    .D(demultiplexer_2_out31), .en(demultiplexer_1_out31), .clk(clock_1_out), .Q(register_23_q));  // open: clr
  // Probe on v0_q
  // Probe on register_1_q
  // Probe on five_q
  // Probe on register_2_q
  // Probe on register_3_q
  // Probe on register_12_q
  // Probe on ten_q
  Register #(.width(32)) register_24 (.D({32{1'b1}}), .Q(register_24_q));  // open: en, clk, clr
  // Probe on register_11_q
  // Probe on register_21_q
  // Probe on register_22_q
  // Probe on register_23_q
  // Probe on register_9_q
  Multiplexer #(.select(5), .width(32)) multiplexer_1 (
    .in0(register_24_q), .in1(at_q), .in2(v0_q), .in3(register_4_q), .in4(register_1_q), .in5(five_q),
    .in6(register_2_q), .in7(register_5_q), .in8(register_3_q), .in9(register_12_q), .in10(ten_q),
    .in11(register_13_q), .in12(register_6_q), .in13(register_14_q), .in14(register_7_q), .in15(fifteen_q),
    .in16(register_8_q), .in17(register_15_q), .in18(register_9_q), .in19(register_16_q), .in20(twenty_q),
    .in21(register_17_q), .in22(register_10_q), .in23(register_18_q), .in24(register_11_q),
    .in25(twentyfive_q), .in26(register_19_q), .in27(register_21_q), .in28(register_20_q),
    .in29(register_22_q), .in30(thirty_q), .in31(register_23_q), .out(rs_out), .sel(rs_select));
  Multiplexer #(.select(5), .width(32)) multiplexer_2 (
    .in0(register_24_q), .in1(at_q), .in2(v0_q), .in3(register_4_q), .in4(register_1_q), .in5(five_q),
    .in6(register_2_q), .in7(register_5_q), .in8(register_3_q), .in9(register_12_q), .in10(ten_q),
    .in11(register_13_q), .in12(register_6_q), .in13(register_14_q), .in14(register_7_q), .in15(fifteen_q),
    .in16(register_8_q), .in17(register_15_q), .in18(register_9_q), .in19(register_16_q), .in20(twenty_q),
    .in21(register_17_q), .in22(register_10_q), .in23(register_18_q), .in24(register_11_q),
    .in25(twentyfive_q), .in26(register_19_q), .in27(register_21_q), .in28(register_20_q),
    .in29(register_22_q), .in30(thirty_q), .in31(register_23_q), .out(rt_out), .sel(rt_select));

  // Notes on the sheet:
  //   rs multiplexer
  //   rt multiplexer
  //   clean these 2 multiplexers
endmodule

module ALU (
  input  WE_control,
  input  [31:0] In1,
  input  [31:0] In2,
  input  [4:0] shamnt,
  input  [3:0] ALU_select,
  output [31:0] ALUout,
  output Beq
);

  wire bit_extender_1_out, clock_1_out, comparator_1_lt;
  wire [15:0] HI_q, LOW_q;
  wire [31:0] adder_1_out, bit_extender_2_out, bit_extender_3_out, bit_extender_4_out, divider_1_out,
       multiplexer_1_out, multiplier_1_out, shifter_1_out, shifter_2_out, subtractor_1_out;

  Clock clock_1 (.out(clock_1_out));
  Adder #(.width(32)) adder_1 (.a(In1), .b(In2), .out(adder_1_out));  // open: cin, cout
  Subtractor #(.width(32)) subtractor_1 (.a(In1), .b(In2), .out(subtractor_1_out));  // open: bin, bout
  Multiplier #(.width(32)) multiplier_1 (.a(In1), .b(In2), .out(multiplier_1_out));  // open: cin, cout
  Divider #(.width(32)) divider_1 (.a(In1), .b(In2), .out(divider_1_out));  // open: upper, rem
  Shifter #(.width(32)) shifter_1 (.in(In2), .\dist (shamnt), .out(shifter_1_out));
  Shifter #(.shift("lr"), .width(32)) shifter_2 (.in(In2), .\dist (shamnt), .out(shifter_2_out));
  Comparator #(.width(32)) comparator_1 (.a(In1), .b(In2), .eq(Beq), .lt(comparator_1_lt));  // open: gt
  Multiplexer #(.width(32)) multiplexer_1 (
    .in0(multiplier_1_out), .in1(divider_1_out), .out(multiplexer_1_out), .sel(bit_extender_1_out));
  // Probe on shifter_1_out
  // Probe on shifter_2_out
  // Probe on multiplexer_1_out[15:0]
  // Probe on multiplexer_1_out[31:16]
  Bit_Extender #(.in_width(4), .out_width(1)) bit_extender_1 (.in(ALU_select), .out(bit_extender_1_out));
  assign bit_extender_2_out = {{31{1'b0}}, comparator_1_lt};  // Bit_Extender bit_extender_2
  Register #(.width(16)) LOW (.D(multiplexer_1_out[15:0]), .en(WE_control), .clk(clock_1_out), .Q(LOW_q));  // open: clr
  Register #(.width(16)) HI (.D(multiplexer_1_out[31:16]), .en(WE_control), .clk(clock_1_out), .Q(HI_q));  // open: clr
  // Probe on LOW_q
  assign bit_extender_3_out = {{16{LOW_q[15]}}, LOW_q};  // Bit_Extender bit_extender_3
  assign bit_extender_4_out = {{16{HI_q[15]}}, HI_q};  // Bit_Extender bit_extender_4
  // Probe on bit_extender_2_out
  // Probe on ALU_select
  // Probe on ALUout
  Multiplexer #(.select(4), .width(32)) multiplexer_2 (
    .in2(adder_1_out), .in3(subtractor_1_out), .in5(bit_extender_3_out), .in6(bit_extender_4_out),
    .in7(shifter_1_out), .in8(shifter_2_out), .in9(bit_extender_2_out), .out(ALUout), .sel(ALU_select));  // open: in0, in1, in4, in10, in11, in12, in13, in14, in15

  // Notes on the sheet:
  //   Branches
  //   clean this ALU
endmodule

module Control (
  input  [31:0] Instruction,
  output [25:0] Jump_offset,
  output jump_select,
  output jalr_jr_select,
  output WE,
  output RegFileWE,
  output [4:0] shamnt,
  output Mem_WE,
  output [15:0] immediate,
  output Mem_select,
  output imm_select,
  output [5:0] Br_select,
  output [3:0] ALU_select,
  output [4:0] rs_select,
  output [4:0] rt_select,
  output [4:0] rd_select
);

  wire comparator_1_eq, control_inner_1_jalr_jr_select, control_inner_1_jump_select;
  wire [4:0] control_inner_1_rd_select;

  Comparator #(.width(32)) comparator_1 (.a(Instruction), .b(32'hc), .eq(comparator_1_eq));  // open: gt, lt
  Multiplexer #(.width(5)) multiplexer_1 (
    .in0(control_inner_1_rd_select), .in1(5'b11010), .out(rd_select), .sel(comparator_1_eq));
  control_inner control_inner_1 (
    .Jump_offset(Jump_offset), .rt_select(rt_select), .rd_select(control_inner_1_rd_select),
    .jump_select(control_inner_1_jump_select), .Mem_WE(Mem_WE), .WE(WE), .Mem_select(Mem_select),
    .jalr_jr_select(control_inner_1_jalr_jr_select), .RegFileWE(RegFileWE), .imm_select(imm_select),
    .ALU_select(ALU_select), .rs_select(rs_select), .Br_select(Br_select), .shamnt(shamnt),
    .immediate(immediate), .Instruction(Instruction));
  Multiplexer multiplexer_2 (.in0(control_inner_1_jump_select), .in1(1'b1), .out(jump_select), .sel(comparator_1_eq));
  Multiplexer multiplexer_3 (
    .in0(control_inner_1_jalr_jr_select), .in1(1'b1), .out(jalr_jr_select), .sel(comparator_1_eq));

  // Notes on the sheet:
  //   syscall
endmodule

module Processor (
  input  [31:0] data_bus_in,
  output mem_we,
  output data_bus_we,
  output [31:0] data_bus_out,
  output [15:0] addr
);

  wire alu_1_beq, branch_helper_1_br_select, control_1_imm_select, control_1_jalr_jr_select,
       control_1_jump_select, control_1_mem_select, control_1_regfilewe, control_1_we, or_1_out;
  wire [3:0] control_1_alu_select;
  wire [4:0] control_1_rd_select, control_1_rs_select, control_1_rt_select, control_1_shamnt;
  wire [5:0] control_1_br_select;
  wire [15:0] control_1_immediate, prog_counter_1_adr_out;
  wire [25:0] control_1_jump_offset;
  wire [31:0] alu_1_aluout, bit_extender_1_out, inst_memory_1_data, multiplexer_1_out, multiplexer_2_out,
       multiplexer_3_out, prog_counter_1_jal, regfile_1_rs_out;

  Inst_Memory inst_memory_1 (.Data(inst_memory_1_data), .Adr(prog_counter_1_adr_out));
  Prog_counter prog_counter_1 (
    .jal(prog_counter_1_jal), .adr_out(prog_counter_1_adr_out), .jump_offset(control_1_jump_offset),
    .jump_select(control_1_jump_select), .Jalr_Jr(regfile_1_rs_out),
    .jalr_jr_select(control_1_jalr_jr_select), .BR_select(branch_helper_1_br_select));
  // Probe on prog_counter_1_jal
  or or_1 (or_1_out, control_1_jump_select, control_1_jalr_jr_select);
  Multiplexer #(.width(32)) multiplexer_1 (
    .in0(multiplexer_3_out), .in1(prog_counter_1_jal), .out(multiplexer_1_out), .sel(or_1_out));
  // Probe on inst_memory_1_data
  // Probe on multiplexer_1_out
  // Probe on control_1_rd_select
  // Probe on control_1_rs_select
  // Probe on control_1_rt_select
  RegFile regfile_1 (
    .rs_out(regfile_1_rs_out), .rt_out(data_bus_out), .rd_select(control_1_rd_select),
    .rs_select(control_1_rs_select), .rt_select(control_1_rt_select), .write_enable(control_1_regfilewe),
    .rd_in(multiplexer_1_out));
  // Probe on control_1_immediate
  // Probe on data_bus_out
  assign bit_extender_1_out = {{16{control_1_immediate[15]}}, control_1_immediate};  // Bit_Extender bit_extender_1
  Control control_1 (
    .rt_select(control_1_rt_select), .rd_select(control_1_rd_select), .ALU_select(control_1_alu_select),
    .Mem_select(control_1_mem_select), .WE(control_1_we), .RegFileWE(control_1_regfilewe),
    .Mem_WE(data_bus_we), .Br_select(control_1_br_select), .shamnt(control_1_shamnt),
    .rs_select(control_1_rs_select), .jump_select(control_1_jump_select),
    .jalr_jr_select(control_1_jalr_jr_select), .imm_select(control_1_imm_select),
    .immediate(control_1_immediate), .Jump_offset(control_1_jump_offset), .Instruction(inst_memory_1_data));
  Multiplexer #(.width(32)) multiplexer_2 (
    .in0(data_bus_out), .in1(bit_extender_1_out), .out(multiplexer_2_out), .sel(control_1_imm_select));
  // Probe on regfile_1_rs_out
  // Probe on multiplexer_2_out
  Multiplexer #(.width(32)) multiplexer_3 (
    .in0(alu_1_aluout), .in1(data_bus_in), .out(multiplexer_3_out), .sel(control_1_mem_select));
  Branch_helper branch_helper_1 (.BR_select(branch_helper_1_br_select), .BR(control_1_br_select), .BEQ_BNE(alu_1_beq));
  ALU alu_1 (
    .ALUout(alu_1_aluout), .Beq(alu_1_beq), .ALU_select(control_1_alu_select), .shamnt(control_1_shamnt),
    .WE_control(control_1_we), .In1(regfile_1_rs_out), .In2(multiplexer_2_out));
  Bit_Extender #(.in_width(32)) bit_extender_2 (.in(alu_1_aluout), .out(addr));

  assign mem_we = data_bus_we;

  // Notes on the sheet:
  //   for Jumps and Branches
  //   for jalr
  //   Zohaib & Ying
endmodule

module Memory (
  input  [15:0] adr,
  input  WE,
  input  [31:0] Data_bus_in,
  output [31:0] Data_bus_out,
  output data_bus_we
);

  wire clock_1_out, comparator_1_eq, multiplexer_2_out, not_1_out;
  wire [15:0] shifter_1_out;

  not not_1 (not_1_out, WE);
  Comparator comparator_1 (.a(adr[15:8]), .b({8{1'b0}}), .eq(comparator_1_eq));  // open: gt, lt
  Multiplexer multiplexer_1 (.in0(not_1_out), .in1(1'b0), .out(data_bus_we), .sel(comparator_1_eq));
  Multiplexer multiplexer_2 (.in0(WE), .in1(1'b0), .out(multiplexer_2_out), .sel(comparator_1_eq));
  Shifter #(.shift("lr"), .width(16)) shifter_1 (.in(adr), .\dist (4'b0010), .out(shifter_1_out));
  Clock clock_1 (.out(clock_1_out));
  // Probe on shifter_1_out
  RAM #(.addrWidth(16), .dataWidth(32), .enables("line")) ram_1 (
    .addr(shifter_1_out), .we(multiplexer_2_out), .clk(clock_1_out), .din(Data_bus_in), .dout(Data_bus_out));

  // Notes on the sheet:
  //   only when we have lw
endmodule

module Inst_Memory (
  input  [15:0] Adr,
  output [31:0] Data
);

  // Probe on Adr
  ROM #(.addrWidth(16), .dataWidth(32)) rom_1 (.addr(Adr), .data(Data));
  Clock clock_1 ();  // open: out
  // Probe on Data

  // Notes on the sheet:
  //   contents of rom_1 (hex, n*v repeats v):
  //   2008000a 2009000c 200a0012 10400019 10480002 10490002 104a000c 8000007 20080010 8d090000 11200006
  //   20080014 8d020000 20080010 20090000 ad090000 8000012 20020000 3400008 20080020 ad040000 20080024
  //   ad050000 20080028 ad060000 2008002c 20090001 ad090000 3400008 2008f000 84080 3a8e820 20100001
  //   20110000 22440000 22650000 228600ff 20020012 c 2002000c c 1040fffd 20080077 10480006 20080061
  //   10480007 20080073 10480008 20080064 10480009 20100000 2011ffff 800003e 2010ffff 20110000 800003e
  //   20100000 20110001 800003e 20100001 20110000 800003e 2509020 2719820 201400ff 22480000 22690001
  //   200a0040 10a0018 4012 1094020 200b0001 10b4022 84080 3a84020 8d0a0000 200b0001 114b0007 ad0b0000
  //   22440000 22650000 22860000 20020012 c 8000027 2002000a c
endmodule

module Prog_counter (
  input  jump_select,
  input  BR_select,
  input  [25:0] jump_offset,
  input  [31:0] Jalr_Jr,
  input  jalr_jr_select,
  output [15:0] adr_out,
  output [31:0] jal
);

  wire clock_1_out;
  wire [15:0] bit_extender_1_out;
  wire [25:0] shifter_1_out;
  wire [31:0] adder_1_out, adder_2_out, bit_extender_2_out, bit_extender_3_out, multiplexer_2_out,
       multiplexer_3_out, register_1_q, shifter_2_out;

  Adder #(.width(32)) adder_1 (.a(32'h4), .b(register_1_q), .out(adder_1_out));  // open: cin, cout
  Bit_Extender #(.in_width(26)) bit_extender_1 (.in(shifter_1_out), .out(bit_extender_1_out));
  // Probe on adder_1_out
  Adder #(.width(32)) adder_2 (.a(adder_1_out), .b(bit_extender_2_out), .out(adder_2_out));  // open: cin, cout
  assign bit_extender_2_out = {{16{bit_extender_1_out[15]}}, bit_extender_1_out};  // Bit_Extender bit_extender_2
  // Probe on bit_extender_1_out
  Shifter #(.width(26)) shifter_1 (.in(jump_offset), .\dist (5'b00010), .out(shifter_1_out));
  Multiplexer #(.width(32)) multiplexer_1 (.in0(adder_1_out), .in1(adder_2_out), .out(jal), .sel(BR_select));
  assign bit_extender_3_out = {{6{shifter_1_out[25]}}, shifter_1_out};  // Bit_Extender bit_extender_3
  // Probe on jal
  Multiplexer #(.width(32)) multiplexer_2 (
    .in0(bit_extender_3_out), .in1(Jalr_Jr), .out(multiplexer_2_out), .sel(jalr_jr_select));
  Multiplexer #(.width(32)) multiplexer_3 (
    .in0(jal), .in1(multiplexer_2_out), .out(multiplexer_3_out), .sel(jump_select));
  // Probe on multiplexer_2_out
  Register #(.width(32)) register_1 (
    .D(multiplexer_3_out), .en(1'b1), .clk(clock_1_out), .Q(register_1_q));  // open: clr
  Clock clock_1 (.out(clock_1_out));
  // Probe on register_1_q
  // Probe on register_1_q
  Shifter #(.shift("lr"), .width(32)) shifter_2 (.in(register_1_q), .\dist (5'b00010), .out(shifter_2_out));
  Bit_Extender #(.in_width(32)) bit_extender_4 (.in(shifter_2_out), .out(adr_out));

  // Notes on the sheet:
  //   clean this 
endmodule

module Branch_helper (
  input  BEQ_BNE,
  input  [5:0] BR,
  output BR_select
);

  wire BEQ_out, BNE_out, comparator_1_eq, comparator_2_eq, not_1_out;

  Comparator #(.width(6)) comparator_1 (.a(BR), .b(6'b000100), .eq(comparator_1_eq));  // open: gt, lt
  Comparator #(.width(6)) comparator_2 (.a(BR), .b(6'b000101), .eq(comparator_2_eq));  // open: gt, lt
  and BEQ (BEQ_out, comparator_1_eq, BEQ_BNE);
  or or_1 (BR_select, BEQ_out, BNE_out);
  and BNE (BNE_out, not_1_out, comparator_2_eq);
  not not_1 (not_1_out, BEQ_BNE);
endmodule

module data_bus (
);

  wire clock_1_out, clock_2_out, keyboard_1_avail, keyboard_controller_1_bus_we,
       keyboard_controller_1_key_read, memory_1_data_bus_we, processor_1_data_bus_we, processor_1_mem_we,
       rgb_video_1_p1, rgb_video_1_p2, terminalcontroller_1_we;
  wire [5:0] rgb_video_1_p3, rgb_video_1_p4;
  wire [6:0] keyboard_1_data, terminalcontroller_1_asciiout;
  wire [15:0] processor_1_addr;
  wire [23:0] rgb_video_1_p5;
  wire [31:0] controlled_buffer_1_out, keyboard_controller_1_data_bus_out, memory_1_data_bus_out,
       processor_1_data_bus_out;

  Clock clock_1 (.out(clock_1_out));
  TTY tty_1 (.data(terminalcontroller_1_asciiout), .clk(clock_2_out), .we(terminalcontroller_1_we));  // open: clr
  Clock clock_2 (.out(clock_2_out));
  TerminalController terminalcontroller_1 (
    .we(terminalcontroller_1_we), .asciiOut(terminalcontroller_1_asciiout), .Addr_in(processor_1_addr),
    .bus_we(processor_1_mem_we), .Data_bus_in(controlled_buffer_1_out));
  // Probe on terminalcontroller_1_asciiout
  // RGB_Video #(.height(64), .width(64)) rgb_video_1: pin names not known; wires that end beside it: rgb_video_1_p1, rgb_video_1_p2, rgb_video_1_p3, rgb_video_1_p4, rgb_video_1_p5
  Clock clock_3 (.out(rgb_video_1_p1));
  Keyboard keyboard_1 (
    .clk(clock_1_out), .re(keyboard_controller_1_key_read), .avail(keyboard_1_avail), .data(keyboard_1_data));  // open: clr
  RGBController rgbcontroller_1 (
    .RGBX(rgb_video_1_p3), .RGBColor(rgb_video_1_p5), .RGBY(rgb_video_1_p4), .RGBWrite(rgb_video_1_p2),
    .WriteEnable(processor_1_mem_we), .DataBusIn(controlled_buffer_1_out), .AddressIn(processor_1_addr));
  assign controlled_buffer_1_out = memory_1_data_bus_we ? memory_1_data_bus_out : 32'bz;  // Controlled_Buffer controlled_buffer_1
  Memory memory_1 (
    .Data_bus_out(memory_1_data_bus_out), .data_bus_we(memory_1_data_bus_we),
    .Data_bus_in(controlled_buffer_1_out), .WE(processor_1_mem_we), .adr(processor_1_addr));
  assign controlled_buffer_1_out = processor_1_data_bus_we ? processor_1_data_bus_out : 32'bz;  // Controlled_Buffer controlled_buffer_2
  Processor processor_1 (
    .data_bus_out(processor_1_data_bus_out), .mem_we(processor_1_mem_we),
    .data_bus_we(processor_1_data_bus_we), .addr(processor_1_addr), .data_bus_in(controlled_buffer_1_out));
  assign controlled_buffer_1_out = keyboard_controller_1_bus_we ? keyboard_controller_1_data_bus_out : 32'bz;  // Controlled_Buffer controlled_buffer_3
  Keyboard_Controller keyboard_controller_1 (
    .key_read(keyboard_controller_1_key_read), .data_bus_out(keyboard_controller_1_data_bus_out),
    .bus_WE(keyboard_controller_1_bus_we), .Addr_in(processor_1_addr), .WE(processor_1_mem_we),
    .data_bus_in(controlled_buffer_1_out), .KeyPressAv(keyboard_1_avail), .Keyboard_in(keyboard_1_data));
  // Probe on controlled_buffer_1_out
  // Probe on processor_1_addr
  // Probe on controlled_buffer_1_out
  // Probe on processor_1_mem_we

  // Notes on the sheet:
  //   Zohaib & Ying
  //   bus_we is 1 for lw
  //   bus_we is 0 for lw
  //   data_out
  //   mem_we
  //   Addr
endmodule

module control_alu_helper (
  input  lw_sw_overwrite,
  input  [5:0] data_in,
  output [3:0] ALU_select,
  output ALU_WE,
  output jalr_jr_select
);

  wire comparator_1_eq, comparator_2_eq, comparator_3_eq, comparator_4_eq, comparator_5_eq, comparator_6_eq,
       comparator_7_eq, comparator_8_eq, comparator_9_eq, comparator_10_eq, comparator_11_eq;
  wire [3:0] multiplexer_1_out, multiplexer_2_out, multiplexer_3_out, multiplexer_4_out, multiplexer_5_out,
       multiplexer_6_out, multiplexer_7_out, multiplexer_8_out, multiplexer_9_out;

  Comparator #(.width(6)) comparator_1 (.a(data_in), .b(6'b100000), .eq(comparator_1_eq));  // open: gt, lt
  Comparator #(.width(6)) comparator_2 (.a(data_in), .b(6'b100010), .eq(comparator_2_eq));  // open: gt, lt
  Comparator #(.width(6)) comparator_3 (.a(data_in), .b(6'b011000), .eq(comparator_3_eq));  // open: gt, lt
  Comparator #(.width(6)) comparator_4 (.a(data_in), .b(6'b011010), .eq(comparator_4_eq));  // open: gt, lt
  Comparator #(.width(6)) comparator_5 (.a(data_in), .b(6'b010000), .eq(comparator_5_eq));  // open: gt, lt
  Comparator #(.width(6)) comparator_6 (.a(data_in), .b(6'b010010), .eq(comparator_6_eq));  // open: gt, lt
  Comparator #(.width(6)) comparator_7 (.a(data_in), .b({6{1'b0}}), .eq(comparator_7_eq));  // open: gt, lt
  Comparator #(.width(6)) comparator_8 (.a(data_in), .b(6'b000010), .eq(comparator_8_eq));  // open: gt, lt
  Comparator #(.width(6)) comparator_9 (.a(data_in), .b(6'b101010), .eq(comparator_9_eq));  // open: gt, lt
  Comparator #(.width(6)) comparator_10 (.a(data_in), .b(6'b001001), .eq(comparator_10_eq));  // open: gt, lt
  Comparator #(.width(6)) comparator_11 (.a(data_in), .b(6'b001000), .eq(comparator_11_eq));  // open: gt, lt
  Multiplexer #(.width(4)) multiplexer_1 (.in1(4'b0010), .out(multiplexer_1_out), .sel(comparator_1_eq));  // open: in0
  or or_1 (ALU_WE, comparator_4_eq, comparator_3_eq);
  xor xor_1 (jalr_jr_select, comparator_10_eq, comparator_11_eq);
  Multiplexer #(.width(4)) multiplexer_2 (
    .in0(multiplexer_1_out), .in1(4'b0011), .out(multiplexer_2_out), .sel(comparator_2_eq));
  Multiplexer #(.width(4)) multiplexer_3 (
    .in0(multiplexer_2_out), .in1(4'b0000), .out(multiplexer_3_out), .sel(comparator_3_eq));
  Multiplexer #(.width(4)) multiplexer_4 (
    .in0(multiplexer_3_out), .in1(4'b0001), .out(multiplexer_4_out), .sel(comparator_4_eq));
  Multiplexer #(.width(4)) multiplexer_5 (
    .in0(multiplexer_4_out), .in1(4'b0110), .out(multiplexer_5_out), .sel(comparator_5_eq));
  Multiplexer #(.width(4)) multiplexer_6 (
    .in0(multiplexer_5_out), .in1(4'b0101), .out(multiplexer_6_out), .sel(comparator_6_eq));
  Multiplexer #(.width(4)) multiplexer_7 (
    .in0(multiplexer_6_out), .in1(4'b0111), .out(multiplexer_7_out), .sel(comparator_7_eq));
  Multiplexer #(.width(4)) multiplexer_8 (
    .in0(multiplexer_7_out), .in1(4'b1000), .out(multiplexer_8_out), .sel(comparator_8_eq));
  Multiplexer #(.width(4)) multiplexer_9 (
    .in0(multiplexer_8_out), .in1(4'b1001), .out(multiplexer_9_out), .sel(comparator_9_eq));
  Multiplexer #(.width(4)) multiplexer_10 (
    .in0(multiplexer_9_out), .in1(4'b0010), .out(ALU_select), .sel(lw_sw_overwrite));

  // Notes on the sheet:
  //   func for add
  //   func for sub
  //   func for mult
  //   func for div
  //   func for mfhi
  //   func for mflo
  //   func for sll
  //   func for srl
  //   func for slt
  //   func for jalr
  //   func for jr
  //   overwrite to add for lw/sw/addi
endmodule

module control_opcode_helper (
  input  [5:0] opcode_in,
  output Mem_we,
  output Mem_select,
  output imm_select,
  output regFile_OW,
  output rd_overwrite
);

  wire comparator_2_eq, comparator_3_eq;

  Comparator #(.width(6)) comparator_1 (.a(opcode_in), .b(6'b101011), .eq(Mem_we));  // open: gt, lt
  Comparator #(.width(6)) comparator_2 (.a(opcode_in), .b(6'b100011), .eq(comparator_2_eq));  // open: gt, lt
  Comparator #(.width(6)) comparator_3 (.a(opcode_in), .b(6'b001000), .eq(comparator_3_eq));  // open: gt, lt
  or or_1 (rd_overwrite, comparator_3_eq, Mem_we, comparator_2_eq);
  or or_2 (Mem_select, Mem_we, comparator_2_eq);
  or or_3 (imm_select, Mem_select, comparator_3_eq);

  assign regFile_OW = Mem_we;

  // Notes on the sheet:
  //   opcode for sw, so imm_select is 1
  //   opcode for lw, so imm_select is 1
  //   opcode for addi, so imm_select is 1
endmodule

module Keyboard_Controller (
  input  [31:0] data_bus_in,
  input  WE,
  input  KeyPressAv,
  input  [6:0] Keyboard_in,
  input  [15:0] Addr_in,
  output key_read,
  output [31:0] data_bus_out,
  output bus_WE
);

  wire and_1_out, comparator_1_eq, comparator_2_eq, comparator_3_eq, comparator_4_eq, multiplexer_3_out,
       not_1_out, or_1_out;
  wire [1:0] multiplexer_5_out;
  wire [6:0] multiplexer_2_out;
  wire [31:0] bit_extender_1_out, bit_extender_2_out;

  // Probe on Addr_in
  // Probe on 16'h10
  not not_1 (not_1_out, WE);
  Comparator #(.width(16)) comparator_1 (.a(Addr_in), .b(16'h10), .eq(comparator_1_eq));  // open: gt, lt
  Multiplexer multiplexer_1 (.in0(1'b0), .in1(not_1_out), .out(bus_WE), .sel(or_1_out));
  or or_1 (or_1_out, comparator_4_eq, comparator_3_eq);
  Multiplexer #(.width(7)) multiplexer_2 (.in0(Keyboard_in), .out(multiplexer_2_out), .sel(WE));  // open: in1
  Multiplexer multiplexer_3 (.in0(KeyPressAv), .out(multiplexer_3_out), .sel(WE));  // open: in1
  Comparator #(.width(32)) comparator_2 (.a(data_bus_in), .b({32{1'b0}}), .eq(comparator_2_eq));  // open: gt, lt
  // Probe on multiplexer_3_out
  // Probe on multiplexer_2_out
  // Probe on bit_extender_1_out
  assign bit_extender_1_out = {{31{1'b0}}, multiplexer_3_out};  // Bit_Extender bit_extender_1
  assign bit_extender_2_out = {{25{1'b0}}, multiplexer_2_out};  // Bit_Extender bit_extender_2
  and and_1 (and_1_out, comparator_1_eq, comparator_2_eq, WE);
  // Probe on bit_extender_2_out
  Comparator #(.width(16)) comparator_3 (.a(Addr_in), .b(16'h14), .eq(comparator_3_eq));  // open: gt, lt
  Multiplexer multiplexer_4 (.in0(1'b0), .in1(1'b1), .out(key_read), .sel(and_1_out));
  Comparator #(.width(16)) comparator_4 (.a(Addr_in), .b(16'h10), .eq(comparator_4_eq));  // open: gt, lt
  Multiplexer #(.width(2)) multiplexer_5 (.in1(2'b01), .out(multiplexer_5_out), .sel(comparator_4_eq));  // open: in0
  Multiplexer #(.width(2)) multiplexer_6 (.in1(2'b10), .out(multiplexer_5_out), .sel(comparator_3_eq));  // open: in0
  Multiplexer #(.select(2), .width(32)) multiplexer_7 (
    .in0({32{1'b0}}), .in1(bit_extender_1_out), .in2(bit_extender_2_out), .out(data_bus_out),
    .sel(multiplexer_5_out));  // open: in3

  // Notes on the sheet:
  //   error here
endmodule

module RGBController (
  input  [15:0] AddressIn,
  input  [31:0] DataBusIn,
  input  WriteEnable,
  output [5:0] RGBX,
  output [5:0] RGBY,
  output [23:0] RGBColor,
  output RGBWrite
);

  wire and_1_out, and_2_out, and_3_out, and_4_out, clock_1_out, comparator_1_eq, comparator_2_eq,
       comparator_3_eq, comparator_4_eq;
  wire [5:0] bit_extender_1_out, bit_extender_2_out;
  wire [23:0] bit_extender_3_out;
  wire [31:0] multiplexer_1_out, multiplexer_2_out, multiplexer_3_out;

  Comparator #(.width(16)) comparator_1 (.a(AddressIn), .b(16'h20), .eq(comparator_1_eq));  // open: gt, lt
  Comparator #(.width(16)) comparator_2 (.a(AddressIn), .b(16'h24), .eq(comparator_2_eq));  // open: gt, lt
  Comparator #(.width(16)) comparator_3 (.a(AddressIn), .b(16'h28), .eq(comparator_3_eq));  // open: gt, lt
  Comparator #(.width(16)) comparator_4 (.a(AddressIn), .b(16'h2c), .eq(comparator_4_eq));  // open: gt, lt
  and and_1 (and_1_out, comparator_1_eq, WriteEnable);
  and and_2 (and_2_out, WriteEnable, comparator_2_eq);
  and and_3 (and_3_out, WriteEnable, comparator_3_eq);
  and and_4 (and_4_out, WriteEnable, comparator_4_eq);
  Multiplexer #(.width(32)) multiplexer_1 (.in1(DataBusIn), .out(multiplexer_1_out), .sel(and_1_out));  // open: in0
  Multiplexer #(.width(32)) multiplexer_2 (.in1(DataBusIn), .out(multiplexer_2_out), .sel(and_2_out));  // open: in0
  Multiplexer #(.width(32)) multiplexer_3 (.in1(DataBusIn), .out(multiplexer_3_out), .sel(and_3_out));  // open: in0
  Multiplexer multiplexer_4 (.in1(WriteEnable), .out(RGBWrite), .sel(and_4_out));  // open: in0
  Bit_Extender #(.in_width(32), .out_width(6)) bit_extender_1 (.in(multiplexer_1_out), .out(bit_extender_1_out));
  Bit_Extender #(.in_width(32), .out_width(6)) bit_extender_2 (.in(multiplexer_2_out), .out(bit_extender_2_out));
  Bit_Extender #(.in_width(32), .out_width(24)) bit_extender_3 (.in(multiplexer_3_out), .out(bit_extender_3_out));
  Register #(.width(6)) X (.D(bit_extender_1_out), .en(and_1_out), .clk(clock_1_out), .Q(RGBX));  // open: clr
  Register #(.width(6)) Y (.D(bit_extender_2_out), .en(and_2_out), .clk(clock_1_out), .Q(RGBY));  // open: clr
  Register #(.width(24)) Color (.D(bit_extender_3_out), .en(and_3_out), .clk(clock_1_out), .Q(RGBColor));  // open: clr
  Clock clock_1 (.out(clock_1_out));
  // Probe on RGBColor
endmodule

module control_inner (
  input  [31:0] Instruction,
  output [5:0] Br_select,
  output jump_select,
  output Mem_WE,
  output Mem_select,
  output imm_select,
  output RegFileWE,
  output [4:0] rt_select,
  output [4:0] rs_select,
  output [4:0] rd_select,
  output [4:0] shamnt,
  output WE,
  output [3:0] ALU_select,
  output jalr_jr_select,
  output [15:0] immediate,
  output [25:0] Jump_offset
);

  wire and_1_out, comparator_1_eq, comparator_2_eq, comparator_3_eq, comparator_4_eq,
       control_opcode_helper_1_rd_overwrite, control_opcode_helper_1_regfile_ow, not_1_out, or_2_out,
       or_3_out, or_4_out, or_5_out, undriven;
  wire [4:0] multiplexer_1_out;
  wire [5:0] multiplexer_3_out;

  Comparator #(.width(6)) comparator_1 (.a(Instruction[31:26]), .b(6'b000010), .eq(comparator_1_eq));  // open: gt, lt
  Comparator #(.width(6)) comparator_2 (.a(Instruction[31:26]), .b(6'b000011), .eq(comparator_2_eq));  // open: gt, lt
  // Probe on Instruction[31:26]
  Multiplexer #(.width(5)) multiplexer_1 (
    .in0(Instruction[15:11]), .in1({5{1'b1}}), .out(multiplexer_1_out), .sel(comparator_2_eq));
  // Probe on Instruction[5:0]
  // Probe on Instruction[15:0]
  // Probe on Instruction[25:0]
  Comparator #(.width(6)) comparator_3 (.a(Instruction[31:26]), .b(6'b000100), .eq(comparator_3_eq));  // open: gt, lt
  Comparator #(.width(6)) comparator_4 (.a(Instruction[31:26]), .b(6'b000101), .eq(comparator_4_eq));  // open: gt, lt
  or or_1 (jump_select, comparator_1_eq, jalr_jr_select, comparator_2_eq);
  or or_2 (or_2_out, comparator_3_eq, comparator_4_eq);
  and and_1 (and_1_out, undriven, not_1_out);
  not not_1 (not_1_out, imm_select);
  Multiplexer #(.width(5)) multiplexer_2 (
    .in0(multiplexer_1_out), .in1(Instruction[20:16]), .out(rd_select),
    .sel(control_opcode_helper_1_rd_overwrite));
  or or_3 (or_3_out, comparator_2_eq, comparator_1_eq);
  or or_4 (or_4_out, or_3_out, or_2_out, imm_select);
  Multiplexer #(.width(6)) multiplexer_3 (
    .in0(Instruction[5:0]), .in1({6{1'b0}}), .out(multiplexer_3_out), .sel(or_4_out));
  control_opcode_helper control_opcode_helper_1 (
    .Mem_select(Mem_select), .imm_select(imm_select), .rd_overwrite(control_opcode_helper_1_rd_overwrite),
    .Mem_we(Mem_WE), .regFile_OW(control_opcode_helper_1_regfile_ow), .opcode_in(Instruction[31:26]));
  or or_5 (or_5_out, control_opcode_helper_1_regfile_ow, WE);
  Multiplexer multiplexer_4 (.in0(1'b1), .in1(1'b0), .out(RegFileWE), .sel(or_5_out));
  control_alu_helper control_alu_helper_1 (
    .jalr_jr_select(jalr_jr_select), .ALU_WE(WE), .ALU_select(ALU_select), .lw_sw_overwrite(imm_select),
    .data_in(multiplexer_3_out));

  assign Br_select = Instruction[31:26];
  assign immediate = Instruction[15:0];
  assign Jump_offset = Instruction[25:0];
  assign rs_select = Instruction[25:21];
  assign rt_select = Instruction[20:16];
  assign shamnt = Instruction[10:6];

  // Notes on the sheet:
  //   jal
  //   for jal, store value in reg 31
  //   reg to acces lw value
  //   reg to store value of lw
  //   test this later
  //   this might not be needed now
  //   if we have an offset, we ignore this helper
  //   switches the value of rt and rd
  //   error here
  //   this is for lw/sw/ and addi
  //   overwrite the ALU 
  //   select to add(2) 
  //   when we have lw/sw/addi
  //   0 for save word
endmodule

module TerminalController (
  input  [31:0] Data_bus_in,
  input  [15:0] Addr_in,
  input  bus_we,
  output [6:0] asciiOut,
  output we
);

  wire comparator_1_eq;
  wire [31:0] multiplexer_1_out;

  Comparator #(.width(16)) comparator_1 (.a(Addr_in), .b(16'h30), .eq(comparator_1_eq));  // open: gt, lt
  and and_1 (we, comparator_1_eq, bus_we);
  Multiplexer #(.width(32)) multiplexer_1 (.in0({32{1'b0}}), .in1(Data_bus_in), .out(multiplexer_1_out), .sel(we));
  // Probe on asciiOut
  Bit_Extender #(.in_width(32), .out_width(7)) bit_extender_1 (.in(multiplexer_1_out), .out(asciiOut));
endmodule
